# Fritzing sketch robot (saved by Fritzing 0.9.3b)
breadboards: 1

parts:
  L1 = Solenoid
  L2 = Solenoid
  L3 = Solenoid
  L4 = Solenoid
  Part1 = Arduino Pro Mini v13
  Q1 = NPN-Transistor [package="TO92 [THT]"]

nets:
  N1: L1.pin1, L2.pin1, L3.pin1, L4.pin1, Part1.RAW
  N2: L1.pin2, L2.pin2, L3.pin2, L4.pin2, Q1.C
  N3: Part1.GND, Q1.E
  N4: Part1.D2, Q1.B
